// Logisim project cpu.circ as structural Verilog: 1 circuit, main circuit main
module main (
  input  in_1,
  input  in_2,
  input  in_3,
  input  IRQ
);

  wire clock_1_out, clock_2_out, controlled_buffer_1_out, decoder_1_out0, decoder_1_out1, decoder_1_out3,
       decoder_2_out0, decoder_2_out1, decoder_2_out2, decoder_2_out3, InvClock, IRClk, MainClock,
       OverlapClock, PCClk, PCLoad, PCOe;
  wire [1:0] counter_1_q, PC01;
  wire [3:0] ALUOp;
  wire [4:0] mCodeAL_q, SeqCntr_q;
  wire [7:0] controlled_buffer_4_out, controlled_buffer_5_out, controlled_buffer_6_out, rom_1_data,
       rom_2_data, rom_3_data;
  wire [13:0] PC_q;
  wire [15:0] BUS;
  wire [15:4] IR_q;

  Decoder #(.select(2)) decoder_1 (
    .out0(decoder_1_out0), .out1(decoder_1_out1), .out3(decoder_1_out3), .sel({in_1, in_2}));  // open: out2, en
  Clock clock_1 (.out(clock_1_out));
  Clock #(.highDuration(5), .lowDuration(5)) clock_2 (.out(clock_2_out));
  Register #(.width(16)) IR (.D(BUS), .Q({IR_q, ALUOp}), .clk(IRClk));  // open: en, clr
  assign controlled_buffer_1_out = decoder_1_out0 ? clock_1_out : 1'bz;  // Controlled_Buffer controlled_buffer_1
  assign controlled_buffer_1_out = decoder_1_out1 ? clock_2_out : 1'bz;  // Controlled_Buffer controlled_buffer_2
  assign controlled_buffer_1_out = decoder_1_out3 ? in_3 : 1'bz;  // Controlled_Buffer controlled_buffer_3
  Counter #(.width(5), .max('h1f)) SeqCntr (
    .Q(SeqCntr_q), .clk(MainClock), .clr(controlled_buffer_5_out[1]));  // open: load, D, count, carry
  Counter #(.width(14), .max('h3fff)) PC (
    .load(PCLoad), .D(BUS[15:2]), .Q(PC_q), .clk(PCClk));  // open: count, carry, clr
  Decoder #(.select(2)) decoder_2 (
    .out0(decoder_2_out0), .out1(decoder_2_out1), .out2(decoder_2_out2), .out3(decoder_2_out3),
    .sel(counter_1_q));  // open: en
  Counter #(.width(2), .max('h3)) counter_1 (
    .Q(counter_1_q), .clk(controlled_buffer_1_out));  // open: load, D, count, carry, clr
  Register #(.width(5)) mCodeAL (.D(SeqCntr_q), .Q(mCodeAL_q), .clk(InvClock));  // open: en, clr
  assign BUS = PCOe ? {PC_q, PC01} : 16'bz;  // Controlled_Buffer PCBuf
  or or_1 (MainClock, decoder_2_out0, decoder_2_out1);
  or or_2 (OverlapClock, decoder_2_out1, decoder_2_out2);
  or or_3 (InvClock, decoder_2_out2, decoder_2_out3);
  ROM #(.addrWidth(16)) rom_1 (.addr({IRQ, IR_q[12:4], ALUOp[3], mCodeAL_q}), .data(rom_1_data));  // open: sel
  assign {controlled_buffer_4_out[7:2], PCOe, controlled_buffer_4_out[0]} = MainClock ? rom_1_data : 8'bz;  // Controlled_Buffer controlled_buffer_4
  assign controlled_buffer_5_out = MainClock ? rom_2_data : 8'bz;  // Controlled_Buffer controlled_buffer_5
  ROM #(.addrWidth(16)) rom_2 (.addr({IRQ, IR_q[12:4], ALUOp[3], mCodeAL_q}), .data(rom_2_data));  // open: sel
  assign controlled_buffer_6_out = MainClock ? rom_3_data : 8'bz;  // Controlled_Buffer controlled_buffer_6
  ROM #(.addrWidth(16)) rom_3 (.addr({IRQ, IR_q[12:4], ALUOp[3], mCodeAL_q}), .data(rom_3_data));  // open: sel
  LED led_1 ();  // open: in

  // Notes on the sheet:
  //   contents of rom_1 (hex, n*v repeats v):
  //   0 1 2 3 4 5 6 7 8 9 a b c d e f 10
  //   contents of rom_2 (hex, n*v repeats v):
  //   16*0 2
endmodule
